// Logisim project trafficlight.circ as structural Verilog: 1 circuit, main circuit main
module main (
  input  in_1
);

  wire and_1_out, and_2_out, and_3_out, and_4_out, and_5_out, and_6_out, and_7_out, and_8_out, and_9_out,
       and_10_out, and_11_out, and_12_out, and_13_out, and_14_out, clock_1_out, not_1_out, not_2_out,
       not_3_out, not_4_out, not_5_out, not_6_out, not_7_out, not_8_out, not_9_out, not_10_out, not_11_out,
       not_12_out, not_13_out, not_14_out, not_15_out, not_16_out, not_17_out, not_18_out, not_19_out,
       not_20_out, not_21_out, not_22_out, not_23_out, not_24_out, or_1_out, or_2_out, or_3_out, or_4_out,
       or_5_out, or_6_out, or_7_out, or_8_out, TA_q, TB_q, TC_q, TD_q;

  or or_1 (or_1_out, and_1_out, and_2_out);
  LED G4 (.in(or_1_out));
  LED Y4 (.in(and_3_out));
  LED R4 (.in(or_2_out));
  and and_1 (and_1_out, TA_q, TB_q, not_1_out);
  and and_2 (and_2_out, TA_q, TB_q, not_2_out);
  // Probe on nothing
  not not_1 (not_1_out, TD_q);
  and and_3 (and_3_out, TA_q, TB_q, TC_q, TD_q);
  or or_2 (or_2_out, not_3_out, not_4_out);
  not not_2 (not_2_out, TC_q);
  not not_3 (not_3_out, TA_q);
  not not_4 (not_4_out, TB_q);
  not not_5 (not_5_out, TA_q);
  not not_6 (not_6_out, TD_q);
  not not_7 (not_7_out, TA_q);
  not not_8 (not_8_out, TC_q);
  not not_9 (not_9_out, TA_q);
  not not_10 (not_10_out, TB_q);
  Clock clock_1 (.out(clock_1_out));
  and and_4 (and_4_out, not_5_out, TB_q, not_6_out);
  and and_5 (and_5_out, not_7_out, TB_q, not_8_out);
  and and_6 (and_6_out, not_9_out, TB_q, TC_q, TD_q);
  or or_3 (or_3_out, TA_q, not_10_out);
  T_Flip_Flop TD (.clk(clock_1_out), .T(in_1), .Q(TD_q));  // open: Qn, preset, reset, en
  LED G2 (.in(or_4_out));
  or or_4 (or_4_out, and_4_out, and_5_out);
  LED Y2 (.in(and_6_out));
  LED R2 (.in(or_3_out));
  T_Flip_Flop TC (.clk(clock_1_out), .T(TD_q), .Q(TC_q));  // open: Qn, preset, reset, en
  T_Flip_Flop TB (.clk(clock_1_out), .T(and_7_out), .Q(TB_q));  // open: Qn, preset, reset, en
  and and_7 (and_7_out, TC_q, TD_q);
  not not_11 (not_11_out, TA_q);
  not not_12 (not_12_out, TB_q);
  not not_13 (not_13_out, TD_q);
  not not_14 (not_14_out, TA_q);
  not not_15 (not_15_out, TB_q);
  not not_16 (not_16_out, TC_q);
  not not_17 (not_17_out, TA_q);
  not not_18 (not_18_out, TB_q);
  T_Flip_Flop TA (.clk(clock_1_out), .T(and_11_out), .Q(TA_q));  // open: Qn, preset, reset, en
  and and_8 (and_8_out, not_11_out, not_12_out, not_13_out);
  and and_9 (and_9_out, not_14_out, not_15_out, not_16_out);
  LED Y1 (.in(and_10_out));
  and and_10 (and_10_out, not_17_out, not_18_out, TC_q);
  LED R1 (.in(or_5_out));
  or or_5 (or_5_out, TA_q, TB_q);
  and and_11 (and_11_out, TB_q, and_7_out);
  or or_6 (or_6_out, and_8_out, and_9_out);
  LED G1 (.in(or_6_out));
  not not_19 (not_19_out, TB_q);
  not not_20 (not_20_out, TD_q);
  not not_21 (not_21_out, TB_q);
  not not_22 (not_22_out, TC_q);
  not not_23 (not_23_out, TB_q);
  not not_24 (not_24_out, TA_q);
  and and_12 (and_12_out, TA_q, not_19_out, not_20_out);
  and and_13 (and_13_out, TA_q, not_21_out, not_22_out);
  and and_14 (and_14_out, TA_q, not_23_out, TC_q, TD_q);
  or or_7 (or_7_out, not_24_out, TB_q);
  or or_8 (or_8_out, and_12_out, and_13_out);
  LED G3 (.in(or_8_out));
  LED Y3 (.in(and_14_out));
  LED R3 (.in(or_7_out));
endmodule
